# Fritzing sketch STM32-BMI-I2C (saved by Fritzing 0.9.6b)
breadboards: 1

parts:
  M1 = STM32F103C8T6 blue mini board
  A1 = BMI160 breakout

nets:
  N1: M1.B6, A1.Pin_9
  N2: M1.B7, A1.Pin_10
  N3: A1.Pin_6, A1.Pin_11
  N4: A1.Pin_8, A1.Pin_12

notes:
  This goes to the ST-Link programmer
  Gnd
  SWCLK
  SWDIO
  3.3V
  This goes to a UART-USB converter
  3.3V
  Gnd
  USB-RX (STM32-TX)
  USB-TX (STM32-RX)

custom parts:
  BMI160 breakout: BMI160 Latest Stance Accelerometer Gyroscope module 6 Dof inertial Measurement Sensors.
