# Fritzing sketch STM32-BMI-SPI (saved by Fritzing 0.9.6b)
breadboards: 1

parts:
  M1 = STM32F103C8T6 blue mini board
  A1 = BMI160 breakout

nets:
  N1: M1.A5, A1.Pin_9
  N2: M1.A6, A1.Pin_12
  N3: M1.A7, A1.Pin_10
  N4: M1.B1, A1.Pin_11

notes:
  This goes to the ST-Link programmer
  Gnd
  SWCLK
  SWDIO
  3.3V
  This goes to a UART-USB converter
  3.3V
  Gnd
  USB-RX (STM32-TX)
  USB-TX (STM32-RX)

custom parts:
  BMI160 breakout: BMI160 Latest Stance Accelerometer Gyroscope module 6 Dof inertial Measurement Sensors.
